# Fritzing sketch Untitled Sketch 3 (saved by Fritzing 0.9.3b)

parts:
  Raspberry_Pi_1 = Raspberry Pi 3 [part_number=RPI-3-V1.2]
  L1 = Inductor [package="400 mil [THT]"]
  R1 = Resistor [tolerance=±5% resistance=220 package=THT]
  Q1 = PNP-Transistor [package="TO92 [THT]"]
  L2 = Inductor [package="400 mil [THT]"]
  R2 = Resistor [tolerance=±5% resistance=220 package=THT]
  Q2 = PNP-Transistor [package="TO92 [THT]"]
  R3 = Resistor [tolerance=±5% resistance=220 package=THT]
  R4 = Resistor [tolerance=±5% resistance=220 package=THT]
  R5 = Resistor [tolerance=±5% resistance=220 package=THT]
  R6 = Resistor [tolerance=±5% resistance=220 package=THT]
  R7 = Resistor [tolerance=±5% resistance=220 package=THT]
  Q3 = PNP-Transistor [package="TO92 [THT]"]
  Q4 = PNP-Transistor [package="TO92 [THT]"]
  Q5 = PNP-Transistor [package="TO92 [THT]"]
  Q6 = PNP-Transistor [package="TO92 [THT]"]
  Q7 = PNP-Transistor [package="TO92 [THT]"]
  L3 = Inductor [package="400 mil [THT]"]
  L4 = Inductor [package="400 mil [THT]"]
  L5 = Inductor [package="400 mil [THT]"]
  L6 = Inductor [package="400 mil [THT]"]
  L7 = Inductor [package="400 mil [THT]"]
  Power_plug1 = Power plug

nets (from the breadboard view):
  N1: Raspberry_Pi_1.GND, Q1.B, Q2.B, Q3.B, Q4.B, Q5.B, Q6.B, Q7.B
  N2: L1.pin_0, L2.pin_0, L3.pin_1, L4.pin_1, L5.pin_1, L6.pin_1, L7.pin_1, Power_plug1.GND
  N3: L1.pin_1, R1.Pin_1
  N4: R1.Pin_0, Q1.C
  N5: Q1.E, Q2.C, Q3.E, Q4.E, Q5.C, Q6.E, Q7.C, Power_plug1.VCC
  N6: L2.pin_1, R2.Pin_0
  N7: R2.Pin_1, Q2.E
  N8: R3.Pin_0, L3.pin_0
  N9: R3.Pin_1, Q3.C
  N10: R4.Pin_0, L4.pin_0
  N11: R4.Pin_1, Q4.C
  N12: R5.Pin_0, L5.pin_0
  N13: R5.Pin_1, Q5.E
  N14: R6.Pin_0, L6.pin_0
  N15: R6.Pin_1, Q6.C
  N16: R7.Pin_0, Q7.E
  N17: R7.Pin_1, L7.pin_0
