# Fritzing sketch wire_scheme.src (saved by Fritzing 0.9.3b)

parts:
  Raspberry_Pi_1 = Raspberry Pi 3 [part_number=RPI-3-V1.2]
  L1 = Inductor [package="400 mil [THT]"]
  R1 = Resistor [tolerance=±5% resistance=220 package=THT]
  Q1 = PNP-Transistor [package="TO92 [THT]"]
  Power_plug1 = Power plug
  L2 = Inductor [package="400 mil [THT]"]
  R2 = Resistor [tolerance=±5% resistance=220 package=THT]
  Q2 = PNP-Transistor [package="TO92 [THT]"]
  L3 = Inductor [package="400 mil [THT]"]
  R3 = Resistor [tolerance=±5% resistance=220 package=THT]
  Q3 = PNP-Transistor [package="TO92 [THT]"]
  L4 = Inductor [package="400 mil [THT]"]
  R4 = Resistor [tolerance=±5% resistance=220 package=THT]
  L5 = Inductor [package="400 mil [THT]"]
  R5 = Resistor [tolerance=±5% resistance=220 package=THT]
  L6 = Inductor [package="400 mil [THT]"]
  R6 = Resistor [tolerance=±5% resistance=220 package=THT]
  Q6 = PNP-Transistor [package="TO92 [THT]"]
  L8 = Inductor [package="400 mil [THT]"]
  R8 = Resistor [tolerance=±5% resistance=220 package=THT]
  Q8 = PNP-Transistor [package="TO92 [THT]"]
  Q5 = PNP-Transistor [package="TO92 [THT]"]
  Q4 = PNP-Transistor [package="TO92 [THT]"]

nets:
  N1: Raspberry_Pi_1.GIPO6, Q2.E
  N2: Raspberry_Pi_1.GIPO13, Q8.E
  N3: Raspberry_Pi_1.GIPO19, Q3.E
  N4: Raspberry_Pi_1.GIPO26, Q1.E
  GND: Raspberry_Pi_1.GND, Q1.B, Power_plug1.GND, Q2.B, Q3.B, Q6.B, Q8.B, Q5.B, Q4.B
  N5: Raspberry_Pi_1.GIPO21, Q6.E
  N6: Raspberry_Pi_1.GIPO20, Q5.E
  N7: Raspberry_Pi_1.GIPO16, Q4.E
  N8: L1.pin_0, R1.Pin_1
  N9: L1.pin_1, Power_plug1.VCC, L2.pin_1, L3.pin_1, L4.pin_1, L5.pin_1, L6.pin_1, L8.pin_1
  N10: R1.Pin_0, Q1.C
  N11: L2.pin_0, R2.Pin_1
  N12: R2.Pin_0, Q2.C
  N13: L3.pin_0, R3.Pin_1
  N14: R3.Pin_0, Q3.C
  N15: L4.pin_0, R4.Pin_1
  N16: R4.Pin_0, Q4.C
  N17: L5.pin_0, R5.Pin_1
  N18: R5.Pin_0, Q5.C
  N19: L6.pin_0, R6.Pin_1
  N20: R6.Pin_0, Q6.C
  N21: L8.pin_0, R8.Pin_1
  N22: R8.Pin_0, Q8.C
